// Logisim project cpu.circ as structural Verilog: 15 circuits, main circuit IFU
module CPU (
  input  reset,
  output [31:0] Result
);

  wire _1, _1_prime, _1_prime_prime, _2, _2_prime, _2_prime_prime, _3, _3_prime, _3_prime_prime, _4,
       _4_prime, _4_prime_prime, _5, _5_prime, _5_prime_prime, _6, _6_prime, _6_prime_prime, _7, _7_prime,
       _7_prime_prime, ALUsrc, clk, END, j, MemToReg, MemWrite, PC_sel, RegDst, RegWrite, zero;
  wire [1:0] ALU_sel, EXT_sel;
  wire [4:0] InsADD, multiplexer_1_out, rs, rt;
  wire [5:0] opcode;
  wire [15:0] add;
  wire [31:0] dm_1_out, ext_1_ext32, \gpr_1_读出的寄存器数据out1 , \gpr_1_读出的寄存器数据out2 , multiplexer_2_out,
       multiplexer_3_out;

  Clock u_clk (.out(clk));
  Mcod mcod_1 (
    .opcode(opcode), .funct(add[5:0]), .PC_sel(PC_sel), .ALU_sel(ALU_sel), .Ext_sel(EXT_sel), .j(j),
    .RegDst(RegDst), .MemToReg(MemToReg), .MemWrite(MemWrite), .ALUsrc(ALUsrc), .RegWrite(RegWrite));
  IFU ifu_1 (
    .\npc_sel_判断是否为beq指令 (PC_sel), .\zero_判断两数是否相等 (zero), .j(j), .clk(clk), .ins({opcode, rs, rt, add}),
    .InsADD(InsADD), .reset(reset));
  Comparator #(.width(32)) comparator_1 (.a({opcode, rs, rt, add}), .b({32{1'b0}}), .eq(END));  // open: gt, lt
  Multiplexer #(.width(5), .enable("false")) multiplexer_1 (
    .in0(rt), .in1(add[15:11]), .out(multiplexer_1_out), .sel(RegDst));
  Segment_Single segment_single_1 (
    .A4(InsADD[4]), .A3(InsADD[3]), .A2(InsADD[2]), .A1(InsADD[1]), .A0(InsADD[0]), .a(_1), .b(_2), .c(_3),
    .d(_4), .e(_5), .f(_6), .g(_7));
  Segment_Tens segment_tens_1 (
    .A4(InsADD[4]), .A3(InsADD[3]), .A2(InsADD[2]), .A1(InsADD[1]), .A0(InsADD[0]), .a(_1_prime),
    .b(_2_prime), .c(_3_prime), .d(_4_prime), .e(_5_prime), .f(_6_prime), .g(_7_prime));
  Segment_End segment_end_1 (
    .A0(END), .a(_1_prime_prime), .b(_2_prime_prime), .c(_3_prime_prime), .d(_4_prime_prime),
    .e(_5_prime_prime), .f(_6_prime_prime), .g(_7_prime_prime));
  EXT ext_1 (.imm16(add), .EXT32(ext_1_ext32), .Ext_sel(EXT_sel));
  _7_Segment_Display u_7_segment_display_1 (
    .g(_7_prime), .f(_6_prime), .a(_1_prime), .b(_2_prime), .e(_5_prime), .d(_4_prime), .c(_3_prime));  // open: dp
  GPR gpr_1 (
    .\待写数据Data (multiplexer_2_out), .clk(clk), .RegWrite(RegWrite), .\读出的寄存器数据Out1 (\gpr_1_读出的寄存器数据out1 ),
    .\读出的寄存器数据Out2 (\gpr_1_读出的寄存器数据out2 ), .\WrCtr写寄存器控制 (multiplexer_1_out), .\读寄存器控制RdCtr1 (rs),
    .\读寄存器控制RdCtr2 (rt), .reset(reset));
  Multiplexer #(.width(32), .enable("false")) multiplexer_2 (
    .in0(Result), .in1(dm_1_out), .out(multiplexer_2_out), .sel(MemToReg));
  _7_Segment_Display u_7_segment_display_2 (.g(_7), .f(_6), .a(_1), .b(_2), .e(_5), .d(_4), .c(_3));  // open: dp
  _7_Segment_Display u_7_segment_display_3 (
    .g(_7_prime_prime), .f(_6_prime_prime), .a(_1_prime_prime), .b(_2_prime_prime), .e(_5_prime_prime),
    .d(_4_prime_prime), .c(_3_prime_prime));  // open: dp
  Multiplexer #(.width(32), .enable("false")) multiplexer_3 (
    .in0(\gpr_1_读出的寄存器数据out2 ), .in1(ext_1_ext32), .out(multiplexer_3_out), .sel(ALUsrc));
  ALU alu_1 (.A(\gpr_1_读出的寄存器数据out1 ), .B(multiplexer_3_out), .ALUctr(ALU_sel), .Result(Result), .zero(zero));
  DM dm_1 (
    .MemWrite(MemWrite), .reset(reset), .clk(clk), .out(dm_1_out), .\input (\gpr_1_读出的寄存器数据out2 ),
    .DMadd(Result[4:0]));

  // Other names for the same wires on the sheet: funct[5:0] = add[5:0]; shamt[4:0] = add[10:6]; rd[4:0] = add[15:11]

  // Notes on the sheet:
  //   写入寄存器时数据来源
  //   是否写入寄存器
  //   ALU第二操作数来源
  //   ALU控制信号
  //   00：加法
  //   01：减法
  //   10：与
  //   11：或
  //   拓展方式
  //   是否为BEQ
  //   数据存储器写使能
  //   数据存储器读使能
  //   当前指令行号
  //   数码管为1时代表指令结束
endmodule

module IFU (
  input  reset,
  input  \npc_sel_判断是否为beq指令 ,
  input  \zero_判断两数是否相等 ,
  input  j,
  input  clk,
  output [4:0] InsADD,
  output [31:0] ins
);

  wire _28, _29, _30, _31;
  wire [0:0] and_1_out;
  wire [1:0] or_1_out;
  wire [27:0] adder_1_out;
  wire [31:0] adder_2_out, bit_extender_1_out, multiplexer_1_out, PC_q, shifter_1_out;

  Adder #(.width(32)) adder_1 (
    .a({PC_q[31:7], InsADD, PC_q[1:0]}), .b(32'h4), .out({_31, _30, _29, _28, adder_1_out}));  // open: cin, cout
  assign bit_extender_1_out = {{16{ins[15]}}, ins[15:0]};  // Bit_Extender bit_extender_1
  Adder #(.width(32)) adder_2 (
    .a({_31, _30, _29, _28, adder_1_out}), .b(shifter_1_out), .out(adder_2_out));  // open: cin, cout
  Shifter #(.width(32)) shifter_1 (.in(bit_extender_1_out), .\dist (5'b00010), .out(shifter_1_out));
  and and_1 (and_1_out[0], \npc_sel_判断是否为beq指令 , \zero_判断两数是否相等 );
  Multiplexer #(.select(2), .width(32), .enable("false")) multiplexer_1 (
    .in0({_31, _30, _29, _28, adder_1_out}), .in1(adder_2_out), .in2({_31, _30, _29, _28, ins[25:0], 2'b00}),
    .in3(32'h3000), .out(multiplexer_1_out), .sel(or_1_out));
  assign or_1_out = {2{reset}} | {j, and_1_out[0]};  // OR_Gate or_1, 2 bits wide
  Register #(.width(32)) PC (.D(multiplexer_1_out), .Q({PC_q[31:7], InsADD, PC_q[1:0]}), .clk(clk));  // open: en, clr
  ROM rom_1 (.addr({PC_q[9:7], InsADD}), .data(ins[31:24]));  // open: sel
  ROM rom_2 (.addr({PC_q[9:7], InsADD}), .data(ins[23:16]));  // open: sel
  ROM rom_3 (.addr({PC_q[9:7], InsADD}), .data(ins[15:8]));  // open: sel
  ROM rom_4 (.addr({PC_q[9:7], InsADD}), .data(ins[7:0]));  // open: sel
  // Probe on ins

  // Other names for the same wires on the sheet: imm[15:0] = ins[15:0]; Imm_j[25:0] = ins[25:0]

  // Notes on the sheet:
  //   contents of rom_1 (hex, n*v repeats v):
  //   3c 11 3c 1 1 1 35 35 ae ae 8e 8e 11 3c 11 3c 3c 8 1 1 3c 8
  //   contents of rom_2 (hex, n*v repeats v):
  //   8 28 9 9 49 6b 6b d b a d e 9 9 9 8 9 0 9 6b 9
  //   contents of rom_3 (hex, n*v repeats v):
  //   0 0 0 50 58 58 11*0 c 50 58 0 c
  //   contents of rom_4 (hex, n*v repeats v):
  //   14 14 f 21 23 21 1 0 0 1 0 1 1 14 2 0 0 13 21 23 14
endmodule

module add1 (
  input  Ai,
  input  Bi,
  input  Ci_1,
  output Si,
  output Ci
);

  wire nand_1_out, nand_2_out, xor_1_out;

  xor xor_1 (xor_1_out, Ai, Bi);
  nand nand_1 (nand_1_out, Ai, Bi);
  xor xor_2 (Si, xor_1_out, Ci_1);
  nand nand_2 (nand_2_out, xor_1_out, Ci_1);
  nand nand_3 (Ci, nand_2_out, nand_1_out);
endmodule

module GPR (
  input  [31:0] \待写数据Data ,
  input  [4:0] \读寄存器控制RdCtr1 ,
  input  reset,
  input  clk,
  input  RegWrite,
  input  [4:0] \WrCtr写寄存器控制 ,
  input  [4:0] \读寄存器控制RdCtr2 ,
  output [31:0] \读出的寄存器数据Out1 ,
  output [31:0] \读出的寄存器数据Out2 
);

  wire demultiplexer_1_out0, demultiplexer_1_out1, demultiplexer_1_out2, demultiplexer_1_out3,
       demultiplexer_1_out4, demultiplexer_1_out5, demultiplexer_1_out6, demultiplexer_1_out7,
       demultiplexer_1_out8, demultiplexer_1_out9, demultiplexer_1_out10, demultiplexer_1_out11,
       demultiplexer_1_out12, demultiplexer_1_out13, demultiplexer_1_out14, demultiplexer_1_out15,
       demultiplexer_1_out16, demultiplexer_1_out17, demultiplexer_1_out18, demultiplexer_1_out19,
       demultiplexer_1_out20, demultiplexer_1_out21, demultiplexer_1_out22, demultiplexer_1_out23,
       demultiplexer_1_out24, demultiplexer_1_out25, demultiplexer_1_out26, demultiplexer_1_out27,
       demultiplexer_1_out28, demultiplexer_1_out29, demultiplexer_1_out30, demultiplexer_1_out31;
  wire [31:0] _0, _1, _2, _3, _4, _5, _6, _7, _8, _9, _10, _11, _12, _13, _14, _15, _16, _17, _18, _19, _20,
       _21, _22, _23, _24, _25, _26, _27, _28, _29, _30, _31;

  Demultiplexer #(.select(5), .enable("false")) demultiplexer_1 (
    .out0(demultiplexer_1_out0), .out1(demultiplexer_1_out1), .out2(demultiplexer_1_out2),
    .out3(demultiplexer_1_out3), .out4(demultiplexer_1_out4), .out5(demultiplexer_1_out5),
    .out6(demultiplexer_1_out6), .out7(demultiplexer_1_out7), .out8(demultiplexer_1_out8),
    .out9(demultiplexer_1_out9), .out10(demultiplexer_1_out10), .out11(demultiplexer_1_out11),
    .out12(demultiplexer_1_out12), .out13(demultiplexer_1_out13), .out14(demultiplexer_1_out14),
    .out15(demultiplexer_1_out15), .out16(demultiplexer_1_out16), .out17(demultiplexer_1_out17),
    .out18(demultiplexer_1_out18), .out19(demultiplexer_1_out19), .out20(demultiplexer_1_out20),
    .out21(demultiplexer_1_out21), .out22(demultiplexer_1_out22), .out23(demultiplexer_1_out23),
    .out24(demultiplexer_1_out24), .out25(demultiplexer_1_out25), .out26(demultiplexer_1_out26),
    .out27(demultiplexer_1_out27), .out28(demultiplexer_1_out28), .out29(demultiplexer_1_out29),
    .out30(demultiplexer_1_out30), .out31(demultiplexer_1_out31), .in(RegWrite), .sel(\WrCtr写寄存器控制 ));
  Register #(.width(32)) register_1 (.D(\待写数据Data ), .en(demultiplexer_1_out0), .Q(_0), .clk(clk), .clr(reset));
  Register #(.width(32)) register_2 (.D(\待写数据Data ), .en(demultiplexer_1_out1), .Q(_1), .clk(clk), .clr(reset));
  Register #(.width(32)) register_3 (.D(\待写数据Data ), .en(demultiplexer_1_out2), .Q(_2), .clk(clk), .clr(reset));
  Register #(.width(32)) register_4 (.D(\待写数据Data ), .en(demultiplexer_1_out3), .Q(_3), .clk(clk), .clr(reset));
  Register #(.width(32)) register_5 (.D(\待写数据Data ), .en(demultiplexer_1_out4), .Q(_4), .clk(clk), .clr(reset));
  Register #(.width(32)) register_6 (.D(\待写数据Data ), .en(demultiplexer_1_out5), .Q(_5), .clk(clk), .clr(reset));
  Register #(.width(32)) register_7 (.D(\待写数据Data ), .en(demultiplexer_1_out6), .Q(_6), .clk(clk), .clr(reset));
  Register #(.width(32)) register_8 (.D(\待写数据Data ), .en(demultiplexer_1_out7), .Q(_7), .clk(clk), .clr(reset));
  Register #(.width(32)) register_9 (.D(\待写数据Data ), .en(demultiplexer_1_out8), .Q(_8), .clk(clk), .clr(reset));
  Register #(.width(32)) register_10 (.D(\待写数据Data ), .en(demultiplexer_1_out9), .Q(_9), .clk(clk), .clr(reset));
  Register #(.width(32)) register_11 (.D(\待写数据Data ), .en(demultiplexer_1_out10), .Q(_10), .clk(clk), .clr(reset));
  Register #(.width(32)) register_12 (.D(\待写数据Data ), .en(demultiplexer_1_out11), .Q(_11), .clk(clk), .clr(reset));
  Register #(.width(32)) register_13 (.D(\待写数据Data ), .en(demultiplexer_1_out12), .Q(_12), .clk(clk), .clr(reset));
  Register #(.width(32)) register_14 (.D(\待写数据Data ), .en(demultiplexer_1_out13), .Q(_13), .clk(clk), .clr(reset));
  Register #(.width(32)) register_15 (.D(\待写数据Data ), .en(demultiplexer_1_out14), .Q(_14), .clk(clk), .clr(reset));
  Register #(.width(32)) register_16 (.D(\待写数据Data ), .en(demultiplexer_1_out15), .Q(_15), .clk(clk), .clr(reset));
  Register #(.width(32)) register_17 (.D(\待写数据Data ), .en(demultiplexer_1_out16), .Q(_16), .clk(clk), .clr(reset));
  Register #(.width(32)) register_18 (.D(\待写数据Data ), .en(demultiplexer_1_out17), .Q(_17), .clk(clk), .clr(reset));
  Register #(.width(32)) register_19 (.D(\待写数据Data ), .en(demultiplexer_1_out18), .Q(_18), .clk(clk), .clr(reset));
  Register #(.width(32)) register_20 (.D(\待写数据Data ), .en(demultiplexer_1_out19), .Q(_19), .clk(clk), .clr(reset));
  Register #(.width(32)) register_21 (.D(\待写数据Data ), .en(demultiplexer_1_out20), .Q(_20), .clk(clk), .clr(reset));
  Register #(.width(32)) register_22 (.D(\待写数据Data ), .en(demultiplexer_1_out21), .Q(_21), .clk(clk), .clr(reset));
  Register #(.width(32)) register_23 (.D(\待写数据Data ), .en(demultiplexer_1_out22), .Q(_22), .clk(clk), .clr(reset));
  Register #(.width(32)) register_24 (.D(\待写数据Data ), .en(demultiplexer_1_out23), .Q(_23), .clk(clk), .clr(reset));
  Register #(.width(32)) register_25 (.D(\待写数据Data ), .en(demultiplexer_1_out24), .Q(_24), .clk(clk), .clr(reset));
  Register #(.width(32)) register_26 (.D(\待写数据Data ), .en(demultiplexer_1_out25), .Q(_25), .clk(clk), .clr(reset));
  Register #(.width(32)) register_27 (.D(\待写数据Data ), .en(demultiplexer_1_out26), .Q(_26), .clk(clk), .clr(reset));
  Register #(.width(32)) register_28 (.D(\待写数据Data ), .en(demultiplexer_1_out27), .Q(_27), .clk(clk), .clr(reset));
  Register #(.width(32)) register_29 (.D(\待写数据Data ), .en(demultiplexer_1_out28), .Q(_28), .clk(clk), .clr(reset));
  Register #(.width(32)) register_30 (.D(\待写数据Data ), .en(demultiplexer_1_out29), .Q(_29), .clk(clk), .clr(reset));
  Register #(.width(32)) register_31 (.D(\待写数据Data ), .en(demultiplexer_1_out30), .Q(_30), .clk(clk), .clr(reset));
  Register #(.width(32)) register_32 (.D(\待写数据Data ), .en(demultiplexer_1_out31), .Q(_31), .clk(clk), .clr(reset));
  Multiplexer #(.select(5), .width(32)) multiplexer_1 (
    .in0(_0), .in1(_1), .in2(_2), .in3(_3), .in4(_4), .in5(_5), .in6(_6), .in7(_7), .in8(_8), .in9(_9),
    .in10(_10), .in11(_11), .in12(_12), .in13(_13), .in14(_14), .in15(_15), .in16(_16), .in17(_17),
    .in18(_18), .in19(_19), .in20(_20), .in21(_21), .in22(_22), .in23(_23), .in24(_24), .in25(_25),
    .in26(_26), .in27(_27), .in28(_28), .in29(_29), .in30(_30), .in31(_31), .out(\读出的寄存器数据Out1 ),
    .sel(\读寄存器控制RdCtr1 ));  // open: en
  Multiplexer #(.select(5), .width(32)) multiplexer_2 (
    .in0(_0), .in1(_1), .in2(_2), .in3(_3), .in4(_4), .in5(_5), .in6(_6), .in7(_7), .in8(_8), .in9(_9),
    .in10(_10), .in11(_11), .in12(_12), .in13(_13), .in14(_14), .in15(_15), .in16(_16), .in17(_17),
    .in18(_18), .in19(_19), .in20(_20), .in21(_21), .in22(_22), .in23(_23), .in24(_24), .in25(_25),
    .in26(_26), .in27(_27), .in28(_28), .in29(_29), .in30(_30), .in31(_31), .out(\读出的寄存器数据Out2 ),
    .sel(\读寄存器控制RdCtr2 ));  // open: en

  // Notes on the sheet:
  //   $v1
  //   $t0
  //   $zero
  //   $at
  //   $v0
  //   $a0
  //   $a1
  //   $a2
  //   $a3
  //   $t1
  //   $t2
  //   $t3
  //   $t4
  //   $t5
  //   $t6
  //   $t7
  //   $s0
  //   $s1
  //   $s2
  //   $s3
  //   $s4
  //   $s5
  //   $s6
  //   $s7
  //   $t8
  //   $t9
  //   $k0
  //   $k1
  //   $gp
  //   $sp
  //   $fp
  //   $ra
endmodule

module ALU (
  input  [31:0] A,
  input  [31:0] B,
  input  [1:0] ALUctr,
  output [31:0] Result,
  output zero
);

  wire [31:0] and_1_out, not_1_out, or_1_out, paraadd32_1_out_3, paraadd32_2_out_3, paraadd32_3_out_3;

  assign not_1_out = ~B;  // NOT_Gate not_1, 32 bits wide
  paraadd32 paraadd32_1 (.in_1(A), .in_2(paraadd32_2_out_3), .out_3(paraadd32_1_out_3));  // open: out_4
  paraadd32 paraadd32_2 (.in_1(32'h1), .in_2(not_1_out), .out_3(paraadd32_2_out_3));  // open: out_4
  assign and_1_out = A & B;  // AND_Gate and_1, 32 bits wide
  assign or_1_out = A | B;  // OR_Gate or_1, 32 bits wide
  Multiplexer #(.select(2), .width(32), .disabled(0)) multiplexer_1 (
    .in0(paraadd32_3_out_3), .in1(paraadd32_1_out_3), .in2(and_1_out), .in3(or_1_out), .out(Result),
    .sel(ALUctr));  // open: en
  paraadd32 paraadd32_3 (.in_1(B), .in_2(A), .out_3(paraadd32_3_out_3));  // open: out_4
  nor nor_1 (zero, Result[31], Result[30], Result[29], Result[28], Result[27], Result[26], Result[25], Result[24], Result[23], Result[22], Result[21], Result[20], Result[19], Result[18], Result[17], Result[16], Result[14], Result[13], Result[12], Result[11], Result[10], Result[9], Result[8], Result[7], Result[6], Result[5], Result[4], Result[3], Result[2], Result[1], Result[0], Result[15]);

  // Notes on the sheet:
  //   ALU控制信号
  //   00：加法
  //   01：减法
  //   10：与
  //   11：或
endmodule

module Mdec (
  input  [5:0] opcode,
  input  [5:0] funct,
  output beq,
  output lui,
  output ori,
  output lw,
  output j,
  output sw,
  output subu,
  output addu
);

  wire nor_1_out, not_1_out, not_2_out, not_3_out, not_4_out, not_5_out, not_6_out, not_7_out, not_8_out,
       not_9_out, not_10_out, not_11_out, not_12_out, not_13_out, not_14_out, not_15_out, not_16_out,
       not_17_out, not_18_out, not_19_out, not_20_out, not_21_out, not_22_out;

  not not_1 (not_1_out, opcode[1]);
  and and_1 (ori, opcode[0], not_1_out, opcode[2], opcode[3], not_9_out, not_5_out);
  nor nor_1 (nor_1_out, opcode[5], opcode[4], opcode[3], opcode[2], opcode[1], opcode[0]);
  not not_2 (not_2_out, funct[2]);
  not not_3 (not_3_out, funct[3]);
  not not_4 (not_4_out, funct[4]);
  not not_5 (not_5_out, opcode[5]);
  not not_6 (not_6_out, opcode[4]);
  not not_7 (not_7_out, opcode[2]);
  not not_8 (not_8_out, funct[1]);
  and and_2 (addu, funct[5], not_4_out, not_3_out, not_2_out, not_8_out, funct[0], nor_1_out);
  and and_3 (lui, opcode[3], not_5_out, not_9_out, opcode[2], opcode[1], opcode[0]);
  not not_9 (not_9_out, opcode[4]);
  and and_4 (sw, not_7_out, not_6_out, opcode[3], opcode[1], opcode[0], opcode[5]);
  and and_5 (beq, not_11_out, not_13_out, not_12_out, not_14_out, not_10_out, opcode[2]);
  not not_10 (not_10_out, opcode[0]);
  not not_11 (not_11_out, opcode[5]);
  not not_12 (not_12_out, opcode[3]);
  not not_13 (not_13_out, opcode[4]);
  not not_14 (not_14_out, opcode[1]);
  not not_15 (not_15_out, opcode[0]);
  not not_16 (not_16_out, opcode[2]);
  not not_17 (not_17_out, opcode[3]);
  and and_6 (subu, nor_1_out, funct[0], funct[1], not_2_out, not_3_out, not_4_out, funct[5]);
  not not_18 (not_18_out, opcode[2]);
  not not_19 (not_19_out, opcode[3]);
  and and_7 (lw, opcode[0], opcode[1], not_18_out, not_20_out, opcode[5], not_19_out);
  not not_20 (not_20_out, opcode[4]);
  not not_21 (not_21_out, opcode[4]);
  not not_22 (not_22_out, opcode[5]);
  and and_8 (j, not_15_out, opcode[1], not_16_out, not_17_out, not_21_out, not_22_out);

  // Notes on the sheet:
  //   lui: pull=down
  //   addu: pull=down
  //   j: pull=down
  //   lw: pull=down
  //   ori: pull=down
  //   sw: pull=down
  //   subu: pull=down
  //   beq: pull=down
endmodule

// Controller
module Mcod (
  input  [5:0] opcode,
  input  [5:0] funct,
  output [1:0] ALU_sel,
  output [1:0] Ext_sel,
  output RegDst,
  output ALUsrc,
  output j,
  output MemToReg,
  output MemWrite,
  output PC_sel,
  output RegWrite
);

  wire add1_1_si, and_2_out, and_4_out, and_5_out, flag, mdec_1_addu, mdec_1_beq, mdec_1_j, mdec_1_lui,
       mdec_1_lw, mdec_1_ori, mdec_1_subu, mdec_1_sw, not_1_out, not_2_out, not_3_out, not_4_out, not_5_out,
       not_6_out, not_7_out, not_8_out, not_9_out, not_10_out, not_11_out, not_12_out, not_13_out,
       not_14_out, not_15_out, not_16_out, not_18_out, not_19_out, or_2_out, or_3_out;
  wire [2:0] multiplexer_1_out, priority_encoder_1_out;

  Mdec mdec_1 (
    .ori(mdec_1_ori), .opcode(opcode), .funct(funct), .lw(mdec_1_lw), .j(mdec_1_j), .sw(mdec_1_sw),
    .subu(mdec_1_subu), .lui(mdec_1_lui), .addu(mdec_1_addu), .beq(mdec_1_beq));
  Priority_Encoder #(.disabled(0)) priority_encoder_1 (
    .in0(mdec_1_addu), .in1(mdec_1_subu), .in2(mdec_1_ori), .in3(mdec_1_lui), .in4(mdec_1_lw),
    .in5(mdec_1_sw), .in6(mdec_1_beq), .in7(mdec_1_j), .out(priority_encoder_1_out), .en_out(flag));  // open: en_in, gs
  and and_1 (ALU_sel[1], not_1_out, multiplexer_1_out[1], not_2_out);
  not not_1 (not_1_out, multiplexer_1_out[2]);
  Multiplexer #(.width(3), .enable("false")) multiplexer_1 (
    .in0(priority_encoder_1_out), .in1(3'b000), .out(multiplexer_1_out), .sel(flag));
  or or_1 (ALU_sel[0], and_2_out, and_4_out);
  and and_2 (and_2_out, multiplexer_1_out[1], not_3_out);
  not not_2 (not_2_out, multiplexer_1_out[0]);
  not not_3 (not_3_out, multiplexer_1_out[0]);
  not not_4 (not_4_out, multiplexer_1_out[2]);
  not not_5 (not_5_out, multiplexer_1_out[0]);
  and and_3 (PC_sel, multiplexer_1_out[2], multiplexer_1_out[1], not_5_out);
  not not_6 (not_6_out, or_2_out);
  or or_2 (or_2_out, multiplexer_1_out[1], multiplexer_1_out[2]);
  and and_4 (and_4_out, not_4_out, not_7_out, multiplexer_1_out[0]);
  not not_7 (not_7_out, multiplexer_1_out[1]);
  not not_8 (not_8_out, multiplexer_1_out[2]);
  not not_9 (not_9_out, multiplexer_1_out[0]);
  not not_10 (not_10_out, multiplexer_1_out[1]);
  and and_5 (and_5_out, not_10_out, not_9_out);
  not not_11 (not_11_out, flag);
  or or_3 (or_3_out, not_8_out, and_5_out);
  and and_6 (RegWrite, or_3_out, not_11_out);
  and and_7 (RegDst, not_6_out, not_12_out);
  not not_12 (not_12_out, flag);
  and and_8 (Ext_sel[1], not_13_out, multiplexer_1_out[1], multiplexer_1_out[0]);
  not not_13 (not_13_out, multiplexer_1_out[2]);
  and and_9 (j, multiplexer_1_out[1], multiplexer_1_out[0], multiplexer_1_out[2]);
  and and_10 (Ext_sel[0], multiplexer_1_out[2], not_14_out);
  not not_14 (not_14_out, multiplexer_1_out[1]);
  not not_15 (not_15_out, multiplexer_1_out[1]);
  not not_16 (not_16_out, multiplexer_1_out[0]);
  and and_11 (MemToReg, multiplexer_1_out[2], not_15_out, not_16_out);
  not not_17 (ALUsrc, add1_1_si);
  add1 add1_1 (.Ai(multiplexer_1_out[1]), .Bi(not_18_out), .Ci_1(1'b0), .Si(add1_1_si));  // open: Ci
  not not_18 (not_18_out, multiplexer_1_out[2]);
  not not_19 (not_19_out, multiplexer_1_out[1]);
  and and_12 (MemWrite, multiplexer_1_out[2], not_19_out, multiplexer_1_out[0]);
endmodule

module EXT (
  input  [15:0] imm16,
  input  [1:0] Ext_sel,
  output [31:0] EXT32
);

  wire [31:0] bit_extender_1_out, bit_extender_2_out;

  assign bit_extender_1_out = {{16{1'b0}}, imm16};  // Bit_Extender bit_extender_1
  assign bit_extender_2_out = {{16{imm16[15]}}, imm16};  // Bit_Extender bit_extender_2
  Multiplexer #(.select(2), .width(32)) multiplexer_1 (
    .in0(bit_extender_1_out), .in1(bit_extender_2_out), .in2({imm16, {16{1'b0}}}), .out(EXT32), .sel(Ext_sel));  // open: in3, en
endmodule

// SegCtr
module Segment_Single (
  input  A4,
  input  A3,
  input  A2,
  input  A1,
  input  A0,
  output a,
  output b,
  output c,
  output d,
  output e,
  output f,
  output g
);

  wire and_1_out, and_2_out, and_3_out, and_4_out, and_5_out, and_6_out, and_7_out, and_8_out, and_9_out,
       and_10_out, and_11_out, and_12_out, and_13_out, and_14_out, and_15_out, and_16_out, and_17_out,
       and_18_out, and_19_out, and_20_out, and_21_out, and_22_out, and_23_out, and_24_out, and_25_out,
       and_26_out, and_27_out, and_28_out, and_29_out, and_30_out, and_31_out, and_32_out, and_33_out,
       and_34_out, and_35_out, and_36_out, and_37_out, and_38_out, and_39_out, and_40_out, and_41_out,
       and_42_out, and_43_out, and_44_out, and_45_out, and_46_out, and_47_out, and_48_out, and_49_out,
       and_50_out, and_51_out, and_52_out, and_53_out, and_54_out, and_55_out, and_56_out, not_1_out,
       not_2_out, not_3_out, not_4_out, not_5_out, not_6_out, not_7_out, not_8_out, not_9_out, not_10_out,
       not_11_out, not_12_out, not_13_out, not_14_out, not_15_out, not_16_out, not_17_out, not_18_out,
       not_19_out, not_20_out, not_21_out, not_22_out, not_23_out, not_24_out, not_25_out, not_26_out,
       not_27_out, not_28_out, not_29_out, not_30_out, not_31_out, not_32_out, not_33_out, not_34_out,
       not_35_out, not_36_out, not_37_out, not_38_out, not_39_out, not_40_out, not_41_out, not_42_out,
       not_43_out, not_44_out, not_45_out, not_46_out, not_47_out, not_48_out, not_49_out, not_50_out,
       not_51_out, not_52_out, not_53_out, not_54_out, not_55_out, not_56_out, not_57_out, not_58_out,
       not_59_out, not_60_out, not_61_out, not_62_out, not_63_out, not_64_out, not_65_out, not_66_out,
       not_67_out, not_68_out, not_69_out, not_70_out, not_71_out, not_72_out, not_73_out, not_74_out,
       not_75_out, not_76_out, not_77_out, not_78_out, not_79_out, not_80_out, not_81_out, not_82_out,
       not_83_out, not_84_out, not_85_out, not_86_out, not_87_out, not_88_out, not_89_out, not_90_out,
       not_91_out, not_92_out, not_93_out, not_94_out, not_95_out, not_96_out, not_97_out, not_98_out;

  not not_1 (not_1_out, A4);
  not not_2 (not_2_out, A2);
  not not_3 (not_3_out, A0);
  not not_4 (not_4_out, A3);
  not not_5 (not_5_out, A4);
  not not_6 (not_6_out, A4);
  not not_7 (not_7_out, A1);
  not not_8 (not_8_out, A1);
  not not_9 (not_9_out, A3);
  not not_10 (not_10_out, A0);
  not not_11 (not_11_out, A2);
  not not_12 (not_12_out, A0);
  not not_13 (not_13_out, A4);
  not not_14 (not_14_out, A2);
  not not_15 (not_15_out, A4);
  not not_16 (not_16_out, A1);
  not not_17 (not_17_out, A0);
  not not_18 (not_18_out, A3);
  not not_19 (not_19_out, A2);
  not not_20 (not_20_out, A3);
  not not_21 (not_21_out, A2);
  not not_22 (not_22_out, A3);
  not not_23 (not_23_out, A2);
  not not_24 (not_24_out, A4);
  not not_25 (not_25_out, A1);
  not not_26 (not_26_out, A4);
  not not_27 (not_27_out, A0);
  not not_28 (not_28_out, A1);
  not not_29 (not_29_out, A0);
  not not_30 (not_30_out, A3);
  not not_31 (not_31_out, A1);
  not not_32 (not_32_out, A2);
  not not_33 (not_33_out, A1);
  not not_34 (not_34_out, A4);
  not not_35 (not_35_out, A3);
  not not_36 (not_36_out, A2);
  not not_37 (not_37_out, A1);
  not not_38 (not_38_out, A4);
  not not_39 (not_39_out, A2);
  not not_40 (not_40_out, A0);
  not not_41 (not_41_out, A3);
  not not_42 (not_42_out, A2);
  not not_43 (not_43_out, A0);
  not not_44 (not_44_out, A3);
  not not_45 (not_45_out, A2);
  not not_46 (not_46_out, A3);
  not not_47 (not_47_out, A0);
  not not_48 (not_48_out, A2);
  not not_49 (not_49_out, A0);
  not not_50 (not_50_out, A4);
  not not_51 (not_51_out, A1);
  not not_52 (not_52_out, A4);
  not not_53 (not_53_out, A1);
  not not_54 (not_54_out, A1);
  not not_55 (not_55_out, A4);
  not not_56 (not_56_out, A3);
  not not_57 (not_57_out, A0);
  not not_58 (not_58_out, A4);
  not not_59 (not_59_out, A2);
  not not_60 (not_60_out, A0);
  not not_61 (not_61_out, A3);
  not not_62 (not_62_out, A2);
  not not_63 (not_63_out, A0);
  not not_64 (not_64_out, A3);
  not not_65 (not_65_out, A0);
  not not_66 (not_66_out, A2);
  not not_67 (not_67_out, A0);
  not not_68 (not_68_out, A4);
  not not_69 (not_69_out, A1);
  not not_70 (not_70_out, A0);
  not not_71 (not_71_out, A0);
  not not_72 (not_72_out, A3);
  not not_73 (not_73_out, A1);
  not not_74 (not_74_out, A0);
  not not_75 (not_75_out, A4);
  not not_76 (not_76_out, A3);
  not not_77 (not_77_out, A1);
  not not_78 (not_78_out, A4);
  not not_79 (not_79_out, A3);
  not not_80 (not_80_out, A0);
  not not_81 (not_81_out, A2);
  not not_82 (not_82_out, A1);
  not not_83 (not_83_out, A0);
  not not_84 (not_84_out, A4);
  not not_85 (not_85_out, A3);
  not not_86 (not_86_out, A2);
  not not_87 (not_87_out, A1);
  not not_88 (not_88_out, A3);
  not not_89 (not_89_out, A2);
  not not_90 (not_90_out, A3);
  not not_91 (not_91_out, A0);
  not not_92 (not_92_out, A4);
  not not_93 (not_93_out, A1);
  not not_94 (not_94_out, A1);
  not not_95 (not_95_out, A4);
  not not_96 (not_96_out, A2);
  not not_97 (not_97_out, A0);
  not not_98 (not_98_out, A3);
  and and_1 (and_1_out, not_1_out, not_2_out, not_3_out);
  and and_2 (and_2_out, not_4_out, A1);
  and and_3 (and_3_out, not_5_out, A2, A0);
  and and_4 (and_4_out, not_6_out, A3, not_7_out);
  and and_5 (and_5_out, A3, A2, not_8_out);
  and and_6 (and_6_out, A4, not_9_out, not_10_out);
  and and_7 (and_7_out, A4, not_11_out, A0);
  and and_8 (and_8_out, A4, A1, not_12_out);
  and and_9 (and_9_out, not_13_out, not_14_out);
  and and_10 (and_10_out, not_15_out, not_16_out, not_17_out);
  and and_11 (and_11_out, not_18_out, not_19_out, A0);
  and and_12 (and_12_out, not_20_out, not_21_out, A1);
  and and_13 (and_13_out, not_22_out, A1, A0);
  and and_14 (and_14_out, not_23_out, A1, A0);
  and and_15 (and_15_out, not_24_out, A3, not_25_out);
  and and_16 (and_16_out, not_26_out, A3, not_27_out);
  and and_17 (and_17_out, A3, not_28_out, not_29_out);
  and and_18 (and_18_out, A4, A2);
  and and_19 (and_19_out, not_30_out, not_31_out);
  and and_20 (and_20_out, not_32_out, not_33_out);
  and and_21 (and_21_out, not_34_out, not_35_out, A2);
  and and_22 (and_22_out, A3, A1);
  and and_23 (and_23_out, A4, not_36_out);
  and and_24 (and_24_out, A4, not_37_out);
  and and_25 (and_25_out, not_38_out, not_39_out, not_40_out);
  and and_26 (and_26_out, not_41_out, not_42_out, not_43_out);
  and and_27 (and_27_out, not_44_out, not_45_out, A1);
  and and_28 (and_28_out, not_46_out, A1, not_47_out);
  and and_29 (and_29_out, not_48_out, A1, not_49_out);
  and and_30 (and_30_out, not_50_out, A2, not_51_out, A0);
  and and_31 (and_31_out, not_52_out, A3, not_53_out);
  and and_32 (and_32_out, A3, not_54_out, A0);
  and and_33 (and_33_out, not_55_out, A3, A2, A0);
  and and_34 (and_34_out, A4, not_56_out, A1);
  and and_35 (and_35_out, A4, A2, not_57_out);
  and and_36 (and_36_out, not_58_out, not_59_out, not_60_out);
  and and_37 (and_37_out, not_61_out, not_62_out, not_63_out);
  and and_38 (and_38_out, not_64_out, A1, not_65_out);
  and and_39 (and_39_out, not_66_out, A1, not_67_out);
  and and_40 (and_40_out, not_68_out, A3, not_69_out, not_70_out);
  and and_41 (and_41_out, A4, A2, not_71_out);
  and and_42 (and_42_out, not_72_out, not_73_out, not_74_out);
  and and_43 (and_43_out, not_75_out, not_76_out, A2, not_77_out);
  and and_44 (and_44_out, not_78_out, not_79_out, A2, not_80_out);
  and and_45 (and_45_out, A3, not_81_out, not_82_out);
  and and_46 (and_46_out, A3, A1, not_83_out);
  and and_47 (and_47_out, not_84_out, A3, A2, A1);
  and and_48 (and_48_out, A4, not_85_out, not_86_out, A1);
  and and_49 (and_49_out, A4, A3, not_87_out);
  and and_50 (and_50_out, not_88_out, not_89_out, A1);
  and and_51 (and_51_out, not_90_out, A1, not_91_out);
  and and_52 (and_52_out, not_92_out, A2, not_93_out);
  and and_53 (and_53_out, A3, not_94_out);
  and and_54 (and_54_out, not_95_out, A3, A2);
  and and_55 (and_55_out, A4, not_96_out, not_97_out);
  and and_56 (and_56_out, A4, not_98_out, A1);
  or or_1 (a, and_1_out, and_2_out, and_3_out, and_4_out, and_5_out, and_6_out, and_7_out, and_8_out);
  or or_2 (b, and_9_out, and_10_out, and_11_out, and_12_out, and_13_out, and_14_out, and_15_out, and_16_out, and_17_out, and_18_out);
  or or_3 (c, and_19_out, and_20_out, A0, and_21_out, and_22_out, and_23_out, and_24_out);
  or or_4 (d, and_25_out, and_26_out, and_27_out, and_28_out, and_29_out, and_30_out, and_31_out, and_32_out, and_33_out, and_34_out, and_35_out);
  or or_5 (e, and_36_out, and_37_out, and_38_out, and_39_out, and_40_out, and_41_out);
  or or_6 (f, and_42_out, and_43_out, and_44_out, and_45_out, and_46_out, and_47_out, and_48_out, and_49_out);
  or or_7 (g, and_50_out, and_51_out, and_52_out, and_53_out, and_54_out, and_55_out, and_56_out);
endmodule

// SegCtr
module Segment_Tens (
  input  A4,
  input  A3,
  input  A2,
  input  A1,
  input  A0,
  output a,
  output b,
  output c,
  output d,
  output e,
  output f,
  output g
);

  wire and_1_out, and_2_out, and_3_out, and_4_out, and_5_out, and_6_out, and_7_out, and_8_out, and_9_out,
       and_10_out, and_11_out, and_12_out, and_13_out, and_14_out, and_15_out, and_16_out, and_17_out,
       and_18_out, and_19_out, not_1_out, not_2_out, not_3_out, not_4_out, not_5_out, not_6_out, not_7_out,
       not_8_out, not_9_out, not_10_out, not_11_out, not_12_out, not_13_out, not_14_out, not_15_out,
       not_16_out, not_17_out, not_18_out, not_19_out, not_20_out, not_21_out, not_22_out, not_23_out,
       not_24_out, not_25_out, not_26_out, not_27_out, not_28_out;

  not not_1 (not_1_out, A4);
  not not_2 (not_2_out, A3);
  not not_3 (not_3_out, A4);
  not not_4 (not_4_out, A2);
  not not_5 (not_5_out, A1);
  not not_6 (not_6_out, A3);
  not not_7 (not_7_out, A3);
  not not_8 (not_8_out, A2);
  not not_9 (not_9_out, A4);
  not not_10 (not_10_out, A3);
  not not_11 (not_11_out, A4);
  not not_12 (not_12_out, A2);
  not not_13 (not_13_out, A1);
  not not_14 (not_14_out, A3);
  not not_15 (not_15_out, A4);
  not not_16 (not_16_out, A3);
  not not_17 (not_17_out, A4);
  not not_18 (not_18_out, A2);
  not not_19 (not_19_out, A1);
  not not_20 (not_20_out, A3);
  not not_21 (not_21_out, A2);
  not not_22 (not_22_out, A1);
  not not_23 (not_23_out, A4);
  not not_24 (not_24_out, A3);
  not not_25 (not_25_out, A4);
  not not_26 (not_26_out, A2);
  not not_27 (not_27_out, A1);
  and and_1 (and_1_out, A4, A2);
  and and_2 (and_2_out, A4, A3);
  and and_3 (and_3_out, not_1_out, not_2_out);
  and and_4 (and_4_out, not_3_out, not_4_out, not_5_out);
  and and_5 (and_5_out, not_6_out, A2);
  and and_6 (and_6_out, A4, A3);
  not not_28 (not_28_out, A4);
  and and_7 (and_7_out, not_7_out, not_8_out);
  and and_8 (and_8_out, A3, A2, A1);
  and and_9 (and_9_out, not_9_out, not_10_out);
  and and_10 (and_10_out, not_11_out, not_12_out, not_13_out);
  and and_11 (and_11_out, not_14_out, A2);
  and and_12 (and_12_out, A4, A3);
  and and_13 (and_13_out, not_15_out, not_16_out);
  and and_14 (and_14_out, not_17_out, not_18_out, not_19_out);
  and and_15 (and_15_out, not_20_out, A2);
  and and_16 (and_16_out, A4, A3, not_21_out);
  and and_17 (and_17_out, A4, A3, not_22_out);
  and and_18 (and_18_out, not_23_out, not_24_out);
  and and_19 (and_19_out, not_25_out, not_26_out, not_27_out);
  or or_1 (g, and_1_out, and_2_out);
  or or_2 (a, and_3_out, and_4_out, and_5_out, and_6_out);
  or or_3 (c, not_28_out, and_7_out, and_8_out);
  or or_4 (d, and_9_out, and_10_out, and_11_out, and_12_out);
  or or_5 (e, and_13_out, and_14_out, and_15_out, and_16_out, and_17_out);
  or or_6 (f, and_18_out, and_19_out);

  assign b = 1'b1;
endmodule

// EngCtr
module Segment_End (
  input  A0,
  output a,
  output b,
  output c,
  output d,
  output e,
  output f,
  output g
);

  not not_1 (a, A0);
  not not_2 (d, A0);
  not not_3 (e, A0);
  not not_4 (f, A0);

  assign b = 1'b1;
  assign c = 1'b1;
  assign g = 1'b0;
endmodule

module DM (
  input  MemWrite,
  input  reset,
  input  clk,
  input  [4:0] DMadd,
  input  [31:0] \input ,
  output [31:0] out
);

  RAM #(.addrWidth(5), .bus("separate")) ram_1 (
    .addr(DMadd), .din(\input [7:0]), .data(out[7:0]), .str(MemWrite), .clk(clk), .clr(reset));  // open: sel, ld
  RAM #(.addrWidth(5), .bus("separate")) ram_2 (
    .addr(DMadd), .din(\input [15:8]), .data(out[15:8]), .str(MemWrite), .clk(clk), .clr(reset));  // open: sel, ld
  RAM #(.addrWidth(5), .bus("separate")) ram_3 (
    .addr(DMadd), .din(\input [23:16]), .data(out[23:16]), .str(MemWrite), .clk(clk), .clr(reset));  // open: sel, ld
  RAM #(.addrWidth(5), .bus("separate")) ram_4 (
    .addr(DMadd), .din(\input [31:24]), .data(out[31:24]), .str(MemWrite), .clk(clk), .clr(reset));  // open: sel, ld

  // Other names for the same wires on the sheet: data_0_7[7:0] = \input [7:0]; data_8_15[7:0] = \input [15:8];
  //   data_16_23[7:0] = \input [23:16]; data_24_31[7:0] = \input [31:24]; dout_0_7[7:0] = out[7:0];
  //   dout_8_15[7:0] = out[15:8]; dout_16_23[7:0] = out[23:16]; dout_24_31[7:0] = out[31:24]
endmodule

module carry8 (
  input  [7:0] D,
  input  CI,
  input  [7:0] T,
  output nC7,
  output nC6,
  output nC5,
  output nC4,
  output nC3,
  output nC2,
  output nC1,
  output nC0
);

  wire and_1_out, and_2_out, and_3_out, and_4_out, and_5_out, and_6_out, and_7_out, and_8_out, and_9_out,
       and_10_out, and_11_out, and_12_out, and_13_out, and_14_out, and_15_out, and_16_out, and_17_out,
       and_18_out, and_19_out, and_20_out, and_21_out, and_22_out, and_23_out, and_24_out, and_25_out,
       and_26_out, and_27_out, and_28_out, and_29_out, and_30_out, and_31_out, and_32_out, and_33_out,
       and_34_out, and_35_out, and_36_out;

  and and_1 (and_1_out, T[7], D[6]);
  and and_2 (and_2_out, T[7], T[6], D[5]);
  and and_3 (and_3_out, T[7], T[6], T[5], D[4]);
  nor C7 (nC7, D[7], and_1_out, and_2_out, and_3_out, and_4_out, and_5_out, and_6_out, and_7_out, and_8_out);
  and and_4 (and_4_out, T[7], T[6], T[5], T[4], D[3]);
  and and_5 (and_5_out, T[7], T[6], T[5], T[4], T[3], D[2]);
  and and_6 (and_6_out, T[7], T[6], T[5], T[4], T[3], T[2], D[1]);
  and and_7 (and_7_out, T[7], T[6], T[5], T[4], T[3], T[2], T[1], D[0]);
  and and_8 (and_8_out, T[7], T[6], T[5], T[4], T[3], T[2], T[1], T[0], CI);
  and and_9 (and_9_out, T[6], T[5], D[4]);
  and and_10 (and_10_out, T[6], D[5]);
  nor C6 (nC6, D[6], and_10_out, and_9_out, and_12_out, and_11_out, and_13_out, and_14_out, and_15_out);
  and and_11 (and_11_out, T[6], T[5], T[4], T[3], D[2]);
  and and_12 (and_12_out, T[6], T[5], T[4], D[3]);
  and and_13 (and_13_out, T[6], T[5], T[4], T[3], T[2], D[1]);
  and and_14 (and_14_out, T[6], T[5], T[4], T[3], T[2], T[1], D[0]);
  and and_15 (and_15_out, T[6], T[5], T[4], T[3], T[2], T[1], T[0], CI);
  and and_16 (and_16_out, T[5], D[4]);
  and and_17 (and_17_out, T[5], T[4], D[3]);
  nor C5 (nC5, D[5], and_16_out, and_17_out, and_18_out, and_20_out, and_19_out, and_21_out);
  and and_18 (and_18_out, T[5], T[4], T[3], D[2]);
  and and_19 (and_19_out, T[5], T[4], T[3], T[2], T[1], D[0]);
  and and_20 (and_20_out, T[5], T[4], T[3], T[2], D[1]);
  and and_21 (and_21_out, T[5], T[4], T[3], T[2], T[1], T[0], CI);
  and and_22 (and_22_out, T[4], T[3], D[2]);
  and and_23 (and_23_out, T[4], D[3]);
  nor C4 (nC4, D[4], and_23_out, and_22_out, and_24_out, and_26_out, and_25_out);
  and and_24 (and_24_out, T[4], T[3], T[2], D[1]);
  and and_25 (and_25_out, T[4], T[3], T[2], T[1], T[0], CI);
  and and_26 (and_26_out, T[4], T[3], T[2], T[1], D[0]);
  and and_27 (and_27_out, T[3], D[2]);
  nor C3 (nC3, D[3], and_27_out, and_28_out, and_29_out, and_30_out);
  and and_28 (and_28_out, T[3], T[2], D[1]);
  and and_29 (and_29_out, T[3], T[2], T[1], D[0]);
  and and_30 (and_30_out, T[3], T[2], T[1], T[0], CI);
  and and_31 (and_31_out, T[2], D[1]);
  nor C2 (nC2, D[2], and_31_out, and_32_out, and_33_out);
  and and_32 (and_32_out, T[2], T[1], D[0]);
  and and_33 (and_33_out, T[2], T[1], T[0], CI);
  nor C1 (nC1, D[1], and_34_out, and_36_out);
  and and_34 (and_34_out, T[1], D[0]);
  nor C0 (nC0, D[0], and_35_out);
  and and_35 (and_35_out, T[0], CI);
  and and_36 (and_36_out, T[1], T[0], CI);

  // Notes on the sheet:
  //   nC6: pull=up
  //   nC2: pull=up
  //   nC7: pull=up
  //   D: pull=down
  //   nC1: pull=up
  //   nC3: pull=up
  //   nC0: pull=up
  //   nC4: pull=up
  //   T: pull=down
  //   nC5: pull=up
endmodule

module paraadd32 (
  input  [31:0] in_1,
  input  [31:0] in_2,
  output [31:0] out_3,
  output out_4
);

  wire add8_1_co, add8_2_co, add8_3_co;
  wire [31:0] nand_1_out, nand_2_out, nand_3_out, nand_4_out, nand_5_out, nand_6_out;

  assign nand_1_out = ~(in_1 & in_2);  // NAND_Gate nand_1, 32 bits wide
  assign nand_2_out = ~(in_1 & nand_3_out);  // NAND_Gate nand_2, 32 bits wide
  assign nand_3_out = ~(in_1 & in_2);  // NAND_Gate nand_3, 32 bits wide
  assign nand_4_out = ~(nand_3_out & in_2);  // NAND_Gate nand_4, 32 bits wide
  assign nand_5_out = ~(nand_1_out & nand_1_out);  // NAND_Gate nand_5, 32 bits wide
  assign nand_6_out = ~(nand_2_out & nand_4_out);  // NAND_Gate nand_6, 32 bits wide
  add8 add8_1 (
    .D(nand_5_out[7:0]), .T(nand_6_out[7:0]), .Ci(1'b0), .A(in_1[7:0]), .B(in_2[7:0]), .out_6(out_3[7:0]),
    .Co(add8_1_co));
  add8 add8_2 (
    .D(nand_5_out[15:8]), .T(nand_6_out[15:8]), .Ci(add8_1_co), .A(in_1[15:8]), .B(in_2[15:8]),
    .out_6(out_3[15:8]), .Co(add8_2_co));
  add8 add8_3 (
    .D(nand_5_out[23:16]), .T(nand_6_out[23:16]), .Ci(add8_2_co), .A(in_1[23:16]), .B(in_2[23:16]),
    .out_6(out_3[23:16]), .Co(add8_3_co));
  add8 add8_4 (
    .D(nand_5_out[31:24]), .T(nand_6_out[31:24]), .Ci(add8_3_co), .A(in_1[31:24]), .B(in_2[31:24]),
    .out_6(out_3[31:24]), .Co(out_4));

  // Notes on the sheet:
  //   out_3: pull=down
  //   in_1: pull=down
  //   in_2: pull=down
  //   out_4: pull=down
  //   A
  //   B
  //   D
  //   T
endmodule

module add8 (
  input  [7:0] D,
  input  [7:0] T,
  input  Ci,
  input  [7:0] A,
  input  [7:0] B,
  output [7:0] out_6,
  output Co
);

  wire carry8_1_nc0, carry8_1_nc1, carry8_1_nc2, carry8_1_nc3, carry8_1_nc4, carry8_1_nc5, carry8_1_nc6,
       carry8_1_nc7, not_1_out, not_3_out, not_4_out, not_5_out, not_6_out, not_7_out, not_8_out;

  carry8 carry8_1 (
    .D(D), .CI(Ci), .T(T), .nC7(carry8_1_nc7), .nC6(carry8_1_nc6), .nC5(carry8_1_nc5), .nC4(carry8_1_nc4),
    .nC3(carry8_1_nc3), .nC2(carry8_1_nc2), .nC1(carry8_1_nc1), .nC0(carry8_1_nc0));
  not not_1 (not_1_out, carry8_1_nc5);
  not not_2 (Co, carry8_1_nc7);
  not not_3 (not_3_out, carry8_1_nc4);
  not not_4 (not_4_out, carry8_1_nc6);
  not not_5 (not_5_out, carry8_1_nc3);
  not not_6 (not_6_out, carry8_1_nc0);
  not not_7 (not_7_out, carry8_1_nc2);
  not not_8 (not_8_out, carry8_1_nc1);
  add1 add1_1 (.Ai(B[0]), .Bi(A[0]), .Ci_1(Ci), .Si(out_6[0]));  // open: Ci
  add1 add1_2 (.Ai(B[1]), .Bi(A[1]), .Ci_1(not_6_out), .Si(out_6[1]));  // open: Ci
  add1 add1_3 (.Ai(B[2]), .Bi(A[2]), .Ci_1(not_8_out), .Si(out_6[2]));  // open: Ci
  add1 add1_4 (.Ai(B[3]), .Bi(A[3]), .Ci_1(not_7_out), .Si(out_6[3]));  // open: Ci
  add1 add1_5 (.Ai(B[4]), .Bi(A[4]), .Ci_1(not_5_out), .Si(out_6[4]));  // open: Ci
  add1 add1_6 (.Ai(B[5]), .Bi(A[5]), .Ci_1(not_3_out), .Si(out_6[5]));  // open: Ci
  add1 add1_7 (.Ai(B[6]), .Bi(A[6]), .Ci_1(not_1_out), .Si(out_6[6]));  // open: Ci
  add1 add1_8 (.Ai(B[7]), .Bi(A[7]), .Ci_1(not_4_out), .Si(out_6[7]));  // open: Ci

  // Notes on the sheet:
  //   T: pull=down
  //   Co: pull=down
  //   out_6: pull=down
  //   B: pull=down
  //   A: pull=down
  //   D: pull=down
  //   Ci: pull=down
endmodule
